# Fritzing sketch Монтажная схема (saved by Fritzing 0.9.10b)

parts:
  WeMos_D1_Mini1 = WeMos D1 Mini
  Pololu_A1 = Pololu A4988 [package=SO16]
  IC1 = Rasberry Pi NIOR Camera [chip_label=IC package="DIP (Dual Inline) [THT]"]  # not connected
  Mod1 = Raspberry Pi 4B  # not connected
  Pololu_A2 = Pololu A4988 [package=SO16]
  M1 = Stepper Motor - Bipolar
  M2 = Stepper Motor - Bipolar
  Power_plug1 = Power plug
  HC-SR04_Sensor_1 = HC-SR04 Ultrasonic Distance Sensor
  C1 = Ceramic Capacitor [capacitance=100nF voltage=35V package="100 mil [THT, multilayer]"]
  S1 = Round Pushbutton
  WS2812B1 = WS2812B 12V Strip -- White (60/m)
  S2 = Limit Switch [package="Breakout Board"]
  U1 = LM2596 step down module

nets:
  N1: WeMos_D1_Mini1.3V3, S2.V
  5V: WeMos_D1_Mini1.5V, Pololu_A1.VMOT, HC-SR04_Sensor_1.VCC, C1.1
  N2: WeMos_D1_Mini1.D0, S2.S
  N3: WeMos_D1_Mini1.D2, WS2812B1.+12V
  N4: WeMos_D1_Mini1.D3, HC-SR04_Sensor_1.TRIG
  N5: WeMos_D1_Mini1.D4, HC-SR04_Sensor_1.ECHO
  N6: WeMos_D1_Mini1.D5, Pololu_A1.DIR
  N7: WeMos_D1_Mini1.D6, Pololu_A1.STEP
  N8: WeMos_D1_Mini1.D7, Pololu_A2.STEP
  N9: WeMos_D1_Mini1.D8, Pololu_A2.DIR
  GND: WeMos_D1_Mini1.G, Pololu_A1.GND, Pololu_A2.GND#8, Power_plug1.GND, HC-SR04_Sensor_1.GND, C1.0, WS2812B1.GND, S2.G, U1.IN-, U1.OUT-
  VDD: Pololu_A1.VDD, Pololu_A2.VDD, S1.leg1, U1.IN+
  N10: Pololu_A1.1B, M2.D
  N11: Pololu_A1.1A, M2.B
  N12: Pololu_A1.2A, M2.C
  N13: Pololu_A1.2B, M2.A
  N14: Pololu_A2.1B, M1.D
  N15: Pololu_A2.1A, M1.B
  N16: Pololu_A2.2A, M1.C
  N17: Pololu_A2.2B, M1.A
  N18: Power_plug1.VCC, S1.leg0
  N19: WS2812B1.DI, U1.OUT+

notes:
  Power Supply Unit проводной
  Питание БП 12в 2а
  LM2596
  Понижающий преобразователь DC DC
  Понижает и стабилизирует питание 12в -> 5в 1,5
  Raspbery Pi 3D+
  Реализует алгоритмы системы технического зрения
  Запитывается по USB
  OV5647
  Камера для Raspberry Pi
  Подключена по шине CSI
  HC-SR04
  УЗ датчик расстояния
  Распознaет наличие грузав зоне сканирования
  WeMos D1mini
  Подключена к Raspberry Pi по USB.
  Используется блокировочный конденсатор на 1мкФ для стабилизации питания
  Nema17HE15-1504S
  Шаговый мотор
  Управление конвеером и лопаткой
  12в 1,5а
  WS2812b
  Световая индикация состояния системы
  SM5-04P
  Определяет конечные позиции лопатки
  TMS2208
  Драйвер шагового двигателя
  1,5а на двигатель

custom parts:
  Rasberry Pi NIOR Camera: Camera
  WS2812B 12V Strip -- White (60/m): WS2812B LED Strip, White, 60 pixels per meter, 12V Power
  Limit Switch: Generic limit switch commonly found on 3D printers. Typical lever microswitch mounted on a PCB board with a 3 pin JST XH connector.
  LM2596 step down module: LM2596 DC-DC step down power supply module 3 A.
